# Fritzing sketch Blood Bowl Timer (saved by Fritzing 0.9.3b)
breadboards: 1

parts:
  Part2 = Arduino Uno (Rev3)
  LCD2 = LCD screen
  R1 = Rotary Potentiometer (Small) [maximum_resistance=100kΩ package=THT]
  S2 = Momentary Switch [package=ksa_sealed_tac_switch]
  S3 = Momentary Switch [package=ksa_sealed_tac_switch]
  J1 = Piezo Speaker
  LED1 = LEDs [package=led10mm]
  LED2 = LEDs [package=led10mm]
  VCC1 = Battery block 9V
  S4 = Toggle Switch [package=THT]

nets:
  N1: Part2.D8, LCD2.E
  N2: Part2.D9_PWM, LCD2.DB4
  N3: Part2.D10_PWM/SS, LCD2.DB5
  N4: Part2.D11_PWM/MOSI, LCD2.DB6
  N5: Part2.D12/MISO, LCD2.DB7
  GND: Part2.GND, LCD2.VSS, LCD2.R/W, LCD2.LED-, R1.leg2, S2.1, S3.1, J1.pin1, LED1.C, LED2.C, VCC1.-
  N6: Part2.D2, J1.pin2
  N7: Part2.D3_PWM, S2.3
  N8: Part2.D4, S3.3
  N9: Part2.D5_PWM, LED1.A
  N10: Part2.D6_PWM, LED2.A
  N11: Part2.D7, LCD2.RS
  5V: Part2.5V, LCD2.VDD, LCD2.LED+, R1.leg1
  N12: Part2.VIN, S4.COM
  N13: LCD2.V0, R1.wiper
  N14: VCC1.+, S4.L1
